// Logisim project CPU.circ as structural Verilog: 4 circuits, main circuit main
module main (
  input  [17:0] in_1,
  input  in_2
);

  wire and_1_out, and_2_out, and_3_out, clock_1_out, D15, I0, I1, I2, I3, not_1_out, T3;
  wire [11:0] instruction_decoder_1_data;
  wire [14:0] instruction_decoder_1_opt_code;

  Clock clock_1 (.out(clock_1_out));
  Timer timer_1 (
    .Clock(clock_1_out), .T3(T3));  // open: Increment, Clear, T0, T1, T2, T4, T5, T6, T7, T8, T9, T10, T11, T12, T13, T14, T15, Overflow
  Instruction_Decoder instruction_decoder_1 (
    ._18_Bit_Input(in_1), .Enable(in_2), .Addressing_Mode({I3, I2, I1, I0}),
    .Opt_Code({D15, instruction_decoder_1_opt_code}), .Data(instruction_decoder_1_data));
  and and_1 (and_1_out, I0, D15, T3);
  and and_2 (and_2_out, instruction_decoder_1_data[0], instruction_decoder_1_data[1], instruction_decoder_1_data[2], instruction_decoder_1_data[3], instruction_decoder_1_data[4], instruction_decoder_1_data[5], instruction_decoder_1_data[6], instruction_decoder_1_data[7], instruction_decoder_1_data[8], instruction_decoder_1_data[9], instruction_decoder_1_data[10], instruction_decoder_1_data[11]);
  and and_3 (and_3_out, and_1_out, not_1_out);
  not not_1 (not_1_out, and_2_out);
  Register #(.width(12)) Accumulator (.clr(and_3_out));  // open: D, en, Q, clk
endmodule

module Timer (
  input  Increment,
  input  Clock,
  input  Clear,
  output T0,
  output T1,
  output T2,
  output T3,
  output T4,
  output T5,
  output T6,
  output T7,
  output T8,
  output T9,
  output T10,
  output T11,
  output T12,
  output T13,
  output T14,
  output T15,
  output Overflow
);

  wire [3:0] counter_1_q;

  Counter #(.width(4), .max('hf)) counter_1 (
    .count(Increment), .Q(counter_1_q), .carry(Overflow), .clk(Clock), .clr(Clear));  // open: load, D
  Decoder #(.select(4)) decoder_1 (
    .out0(T0), .out1(T1), .out2(T2), .out3(T3), .out4(T4), .out5(T5), .out6(T6), .out7(T7), .out8(T8),
    .out9(T9), .out10(T10), .out11(T11), .out12(T12), .out13(T13), .out14(T14), .out15(T15), .sel(counter_1_q));  // open: en
endmodule

module Bus (
  input  [11:0] in_1,
  input  [11:0] in_2,
  input  [11:0] in_3,
  input  [11:0] in_4,
  input  [11:0] in_5,
  input  [11:0] in_6,
  input  [17:0] in_7,
  input  [7:0] in_8,
  input  [7:0] in_9
);

  wire undriven, undriven_2, undriven_3, undriven_4, undriven_5, undriven_6, undriven_7, undriven_8,
       undriven_9;

  Multiplexer #(.select(4)) multiplexer_1 (
    .in0(undriven), .in1(undriven_2), .in2(undriven_3), .in3(undriven_4), .in4(undriven_5), .in5(undriven_8),
    .in6(undriven_6), .in7(undriven_7), .in8(undriven_9));  // open: in9, in10, in11, in12, in13, in14, in15, out, sel, en
endmodule

// ID
module Instruction_Decoder (
  input  [17:0] _18_Bit_Input,
  input  Enable,
  output [3:0] Addressing_Mode,
  output [15:0] Opt_Code,
  output [11:0] Data
);

  Decoder #(.select(2)) decoder_1 (
    .out0(Addressing_Mode[0]), .out1(Addressing_Mode[1]), .out2(Addressing_Mode[2]),
    .out3(Addressing_Mode[3]), .sel(_18_Bit_Input[17:16]), .en(Enable));
  Decoder #(.select(4)) decoder_2 (
    .out0(Opt_Code[0]), .out1(Opt_Code[1]), .out2(Opt_Code[2]), .out3(Opt_Code[3]), .out4(Opt_Code[4]),
    .out5(Opt_Code[5]), .out6(Opt_Code[6]), .out7(Opt_Code[7]), .out8(Opt_Code[8]), .out9(Opt_Code[9]),
    .out10(Opt_Code[10]), .out11(Opt_Code[11]), .out12(Opt_Code[12]), .out13(Opt_Code[13]),
    .out14(Opt_Code[14]), .out15(Opt_Code[15]), .sel(_18_Bit_Input[15:12]), .en(Enable));

  assign Data = _18_Bit_Input[11:0];

  // Other names for the same wires on the sheet: ENB = Enable
endmodule
